// Logisim project alu.circ as structural Verilog: 1 circuit, main circuit alu
module alu (
  input  [31:0] A,
  input  [31:0] B,
  input  [3:0] ALUSel,
  output [31:0] ALUResult
);

  wire comparator_1_lt, comparator_2_lt;
  wire [31:0] ALUSel0, ALUSel1, ALUSel2, ALUSel3, ALUSel4, ALUSel5, ALUSel6, ALUSel7, ALUSel8, ALUSel9,
       ALUSel11, ALUSel12, ALUSel13, multiplier_2_out;
  wire [63:0] bit_extender_1_out, bit_extender_2_out, bit_extender_3_out, bit_extender_4_out;

  Comparator #(.width(32)) comparator_1 (.a(A), .b(B), .lt(comparator_1_lt));  // open: gt, eq
  assign bit_extender_1_out = {{32{A[31]}}, A};  // Bit_Extender bit_extender_1
  Multiplier #(.mode("twosComplement"), .width(64)) multiplier_1 (
    .a(bit_extender_1_out), .b(bit_extender_2_out), .out({ALUSel9, ALUSel8}));  // open: cin, cout
  assign bit_extender_2_out = {{32{B[31]}}, B};  // Bit_Extender bit_extender_2
  assign bit_extender_3_out = {{32{1'b0}}, A};  // Bit_Extender bit_extender_3
  Multiplier #(.mode("twosComplement"), .width(64)) multiplier_2 (
    .a(bit_extender_3_out), .b(bit_extender_4_out), .out({ALUSel11, multiplier_2_out}));  // open: cin, cout
  assign bit_extender_4_out = {{32{1'b0}}, B};  // Bit_Extender bit_extender_4
  Adder #(.width(32)) adder_1 (.a(A), .b(B), .out(ALUSel0));  // open: cin, cout
  Shifter #(.width(32)) shifter_1 (.in(A), .\dist (B[4:0]), .out(ALUSel1));
  assign ALUSel2 = {{31{1'b0}}, comparator_1_lt};  // Bit_Extender bit_extender_5
  assign ALUSel4 = A ^ B;  // XOR_Gate xor_1, 32 bits wide
  Shifter #(.shift("lr"), .width(32)) shifter_2 (.in(A), .\dist (B[4:0]), .out(ALUSel5));
  assign ALUSel6 = A | B;  // OR_Gate or_1, 32 bits wide
  assign ALUSel7 = A & B;  // AND_Gate and_1, 32 bits wide
  Subtractor #(.width(32)) subtractor_1 (.a(A), .b(B), .out(ALUSel12));  // open: bin, bout
  Shifter #(.shift("ar"), .width(32)) shifter_3 (.in(A), .\dist (B[4:0]), .out(ALUSel13));
  Comparator #(.mode("unsigned"), .width(32)) comparator_2 (.a(A), .b(B), .lt(comparator_2_lt));  // open: gt, eq
  assign ALUSel3 = {{31{1'b0}}, comparator_2_lt};  // Bit_Extender bit_extender_6
  Multiplexer #(.select(4), .width(32)) multiplexer_1 (
    .in0(ALUSel0), .in1(ALUSel1), .in2(ALUSel2), .in3(ALUSel3), .in4(ALUSel4), .in5(ALUSel5), .in6(ALUSel6),
    .in7(ALUSel7), .in8(ALUSel8), .in9(ALUSel9), .in11(ALUSel11), .in12(ALUSel12), .in13(ALUSel13), .in15(B),
    .out(ALUResult), .sel(ALUSel));  // open: in10, in14

  // Other names for the same wires on the sheet: ALUSel15[31:0] = B

  // Notes on the sheet:
  //   INPUTS to your circuit
  //   DON'T CHANGE THE LOCATIONS OF THE INPUTS AND OUTPUTS!
  //   OUTPUT from your circuit
endmodule
