// Logisim project control-logic.circ as structural Verilog: 1 circuit, main circuit control_logic
module control_logic (
  input  [31:0] Instruction,
  input  BrEq,
  input  BrLt,
  output PCSel,
  output RegWEn,
  output [2:0] ImmSel,
  output BrUn,
  output ASel,
  output BSel,
  output [3:0] ALUSel,
  output MemRW,
  output [1:0] WBSel
);

  wire addi, addr, and_1_out, and_2_out, and_3_out, and_4_out, and_5_out, and_6_out, and_7_out, and_8_out,
       and_43_out, and_44_out, and_45_out, and_46_out, and_47_out, and_48_out, andi, andr, auipc, beq, bge,
       bgeu, blt, bltu, bne, BPCSel, comparator_1_eq, comparator_2_eq, comparator_3_eq, comparator_4_eq,
       comparator_5_eq, comparator_6_eq, comparator_7_eq, comparator_8_eq, comparator_9_eq, comparator_10_eq,
       comparator_11_eq, comparator_12_eq, comparator_13_eq, comparator_14_eq, comparator_15_eq,
       comparator_16_eq, comparator_17_eq, comparator_18_eq, comparator_19_eq, comparator_20_eq,
       comparator_21_eq, comparator_22_eq, comparator_23_eq, comparator_24_eq, comparator_25_eq,
       comparator_26_eq, comparator_27_eq, comparator_28_eq, comparator_29_eq, comparator_30_eq,
       comparator_31_eq, comparator_32_eq, comparator_33_eq, comparator_34_eq, comparator_35_eq,
       comparator_36_eq, comparator_37_eq, jal, jalr, JPCSel, lb, lh, lui, lw, mulhm, mulhum, mulm,
       not_1_out, not_2_out, not_3_out, not_4_out, not_5_out, not_6_out, or_1_out, or_2_out, or_3_out,
       or_4_out, ori, orr, sb, sh, slli, sllr, slti, sltiu, sltr, sltur, srai, srar, srli, srlr, subr, sw,
       xori, xorr;
  wire [5:0] ROMInput;
  wire [15:14] rom_1_data;

  ROM #(.addrWidth(6), .dataWidth(16)) rom_1 (
    .addr(ROMInput), .data({rom_1_data, WBSel, MemRW, ALUSel, BSel, ASel, BrUn, ImmSel, RegWEn}));
  or or_1 (or_1_out, beq, bne, blt, bge);
  or or_2 (or_2_out, bltu, bgeu);
  or or_3 (or_3_out, lb, lh, lw);
  or or_4 (or_4_out, sb, sh, sw);
  or or_5 (PCSel, BPCSel, JPCSel);
  Priority_Encoder #(.select_enc(6)) priority_encoder_1 (
    .in0(addi), .in1(slti), .in2(sltiu), .in3(xori), .in4(ori), .in5(andi), .in6(slli), .in7(srli),
    .in8(srai), .in9(addr), .in10(subr), .in11(sllr), .in12(sltr), .in13(sltur), .in14(xorr), .in15(srlr),
    .in16(srar), .in17(orr), .in18(andr), .in19(mulm), .in20(mulhm), .in21(mulhum), .in22(or_1_out),
    .in23(or_2_out), .in24(or_3_out), .in25(or_4_out), .in26(jal), .in27(jalr), .in28(auipc), .in29(lui),
    .out(ROMInput));  // open: in30, in31, in32, in33, in34, in35, in36, in37, in38, in39, in40, in41, in42, in43, in44, in45, in46, in47, in48, in49, in50, in51, in52, in53, in54, in55, in56, in57, in58, in59, in60, in61, in62, in63, gs, en_out, en_in
  Comparator #(.width(5)) comparator_1 (.a(Instruction[6:2]), .b(5'b01100), .eq(comparator_1_eq));  // open: gt, lt
  Comparator #(.width(5)) comparator_2 (.a(Instruction[6:2]), .b(5'b00100), .eq(comparator_2_eq));  // open: gt, lt
  Comparator #(.width(3)) comparator_3 (.a(Instruction[14:12]), .b(3'b000), .eq(comparator_3_eq));  // open: gt, lt
  Comparator #(.width(3)) comparator_4 (.a(Instruction[14:12]), .b(3'b010), .eq(comparator_4_eq));  // open: gt, lt
  Comparator #(.width(3)) comparator_5 (.a(Instruction[14:12]), .b(3'b011), .eq(comparator_5_eq));  // open: gt, lt
  Comparator #(.width(3)) comparator_6 (.a(Instruction[14:12]), .b(3'b100), .eq(comparator_6_eq));  // open: gt, lt
  Comparator #(.width(3)) comparator_7 (.a(Instruction[14:12]), .b(3'b110), .eq(comparator_7_eq));  // open: gt, lt
  Comparator #(.width(3)) comparator_8 (.a(Instruction[14:12]), .b(3'b111), .eq(comparator_8_eq));  // open: gt, lt
  Comparator #(.width(3)) comparator_9 (.a(Instruction[14:12]), .b(3'b001), .eq(comparator_9_eq));  // open: gt, lt
  Comparator #(.width(3)) comparator_10 (.a(Instruction[14:12]), .b(3'b101), .eq(comparator_10_eq));  // open: gt, lt
  Comparator #(.width(3)) comparator_11 (.a(Instruction[14:12]), .b(3'b000), .eq(comparator_11_eq));  // open: gt, lt
  Comparator #(.width(3)) comparator_12 (.a(Instruction[14:12]), .b(3'b001), .eq(comparator_12_eq));  // open: gt, lt
  Comparator #(.width(3)) comparator_13 (.a(Instruction[14:12]), .b(3'b010), .eq(comparator_13_eq));  // open: gt, lt
  Comparator #(.width(3)) comparator_14 (.a(Instruction[14:12]), .b(3'b011), .eq(comparator_14_eq));  // open: gt, lt
  Comparator #(.width(3)) comparator_15 (.a(Instruction[14:12]), .b(3'b100), .eq(comparator_15_eq));  // open: gt, lt
  Comparator #(.width(3)) comparator_16 (.a(Instruction[14:12]), .b(3'b101), .eq(comparator_16_eq));  // open: gt, lt
  Comparator #(.width(3)) comparator_17 (.a(Instruction[14:12]), .b(3'b110), .eq(comparator_17_eq));  // open: gt, lt
  Comparator #(.width(3)) comparator_18 (.a(Instruction[14:12]), .b(3'b111), .eq(comparator_18_eq));  // open: gt, lt
  Comparator #(.width(5)) comparator_19 (.a(Instruction[6:2]), .b(5'b01100), .eq(comparator_19_eq));  // open: gt, lt
  Comparator #(.width(3)) comparator_20 (.a(Instruction[14:12]), .b(3'b000), .eq(comparator_20_eq));  // open: gt, lt
  Comparator #(.width(3)) comparator_21 (.a(Instruction[14:12]), .b(3'b001), .eq(comparator_21_eq));  // open: gt, lt
  Comparator #(.width(3)) comparator_22 (.a(Instruction[14:12]), .b(3'b011), .eq(comparator_22_eq));  // open: gt, lt
  Comparator #(.width(5)) comparator_23 (.a(Instruction[6:2]), .b(5'b11000), .eq(comparator_23_eq));  // open: gt, lt
  Comparator #(.width(3)) comparator_24 (.a(Instruction[14:12]), .b(3'b000), .eq(comparator_24_eq));  // open: gt, lt
  Comparator #(.width(3)) comparator_25 (.a(Instruction[14:12]), .b(3'b001), .eq(comparator_25_eq));  // open: gt, lt
  Comparator #(.width(3)) comparator_26 (.a(Instruction[14:12]), .b(3'b100), .eq(comparator_26_eq));  // open: gt, lt
  Comparator #(.width(3)) comparator_27 (.a(Instruction[14:12]), .b(3'b101), .eq(comparator_27_eq));  // open: gt, lt
  Comparator #(.width(3)) comparator_28 (.a(Instruction[14:12]), .b(3'b110), .eq(comparator_28_eq));  // open: gt, lt
  Comparator #(.width(3)) comparator_29 (.a(Instruction[14:12]), .b(3'b111), .eq(comparator_29_eq));  // open: gt, lt
  Comparator #(.width(5)) comparator_30 (.a(Instruction[6:2]), .b({5{1'b0}}), .eq(comparator_30_eq));  // open: gt, lt
  Comparator #(.width(3)) comparator_31 (.a(Instruction[14:12]), .b(3'b000), .eq(comparator_31_eq));  // open: gt, lt
  Comparator #(.width(3)) comparator_32 (.a(Instruction[14:12]), .b(3'b001), .eq(comparator_32_eq));  // open: gt, lt
  Comparator #(.width(3)) comparator_33 (.a(Instruction[14:12]), .b(3'b010), .eq(comparator_33_eq));  // open: gt, lt
  Comparator #(.width(5)) comparator_34 (.a(Instruction[6:2]), .b(5'b01000), .eq(comparator_34_eq));  // open: gt, lt
  Comparator #(.width(3)) comparator_35 (.a(Instruction[14:12]), .b(3'b000), .eq(comparator_35_eq));  // open: gt, lt
  Comparator #(.width(3)) comparator_36 (.a(Instruction[14:12]), .b(3'b001), .eq(comparator_36_eq));  // open: gt, lt
  Comparator #(.width(3)) comparator_37 (.a(Instruction[14:12]), .b(3'b010), .eq(comparator_37_eq));  // open: gt, lt
  Comparator #(.width(5)) comparator_38 (.a(Instruction[6:2]), .b(5'b11011), .eq(jal));  // open: gt, lt
  Comparator #(.width(5)) comparator_39 (.a(Instruction[6:2]), .b(5'b11001), .eq(jalr));  // open: gt, lt
  Comparator #(.width(5)) comparator_40 (.a(Instruction[6:2]), .b(5'b00101), .eq(auipc));  // open: gt, lt
  Comparator #(.width(5)) comparator_41 (.a(Instruction[6:2]), .b(5'b01101), .eq(lui));  // open: gt, lt
  and and_1 (and_1_out, comparator_10_eq, not_1_out);
  not not_1 (not_1_out, Instruction[30]);
  and and_2 (and_2_out, comparator_10_eq, Instruction[30]);
  and and_3 (and_3_out, comparator_1_eq, not_2_out);
  not not_2 (not_2_out, Instruction[25]);
  and and_4 (and_4_out, comparator_11_eq, not_3_out);
  not not_3 (not_3_out, Instruction[30]);
  and and_5 (and_5_out, comparator_11_eq, Instruction[30]);
  and and_6 (and_6_out, comparator_16_eq, not_4_out);
  not not_4 (not_4_out, Instruction[30]);
  and and_7 (and_7_out, comparator_16_eq, Instruction[30]);
  and and_8 (and_8_out, comparator_19_eq, Instruction[25]);
  and and_9 (addi, comparator_2_eq, comparator_3_eq);
  and and_10 (slti, comparator_2_eq, comparator_4_eq);
  and and_11 (sltiu, comparator_2_eq, comparator_5_eq);
  and and_12 (xori, comparator_2_eq, comparator_6_eq);
  and and_13 (ori, comparator_2_eq, comparator_7_eq);
  and and_14 (andi, comparator_2_eq, comparator_8_eq);
  and and_15 (slli, comparator_2_eq, comparator_9_eq);
  and and_16 (srli, comparator_2_eq, and_1_out);
  and and_17 (srai, comparator_2_eq, and_2_out);
  and and_18 (addr, and_3_out, and_4_out);
  and and_19 (subr, and_3_out, and_5_out);
  and and_20 (sllr, and_3_out, comparator_12_eq);
  and and_21 (sltr, and_3_out, comparator_13_eq);
  and and_22 (sltur, and_3_out, comparator_14_eq);
  and and_23 (xorr, and_3_out, comparator_15_eq);
  and and_24 (srlr, and_3_out, and_6_out);
  and and_25 (srar, and_3_out, and_7_out);
  and and_26 (orr, and_3_out, comparator_17_eq);
  and and_27 (andr, and_3_out, comparator_18_eq);
  and and_28 (mulm, and_8_out, comparator_20_eq);
  and and_29 (mulhm, and_8_out, comparator_21_eq);
  and and_30 (mulhum, and_8_out, comparator_22_eq);
  and and_31 (beq, comparator_23_eq, comparator_24_eq);
  and and_32 (bne, comparator_23_eq, comparator_25_eq);
  and and_33 (blt, comparator_23_eq, comparator_26_eq);
  and and_34 (bge, comparator_23_eq, comparator_27_eq);
  and and_35 (bltu, comparator_23_eq, comparator_28_eq);
  and and_36 (bgeu, comparator_23_eq, comparator_29_eq);
  and and_37 (lb, comparator_30_eq, comparator_31_eq);
  and and_38 (lh, comparator_30_eq, comparator_32_eq);
  and and_39 (lw, comparator_30_eq, comparator_33_eq);
  and and_40 (sb, comparator_34_eq, comparator_35_eq);
  and and_41 (sh, comparator_34_eq, comparator_36_eq);
  and and_42 (sw, comparator_34_eq, comparator_37_eq);
  not not_5 (not_5_out, BrEq);
  not not_6 (not_6_out, BrLt);
  and and_43 (and_43_out, BrEq, beq);
  and and_44 (and_44_out, not_5_out, bne);
  and and_45 (and_45_out, BrLt, blt);
  and and_46 (and_46_out, not_6_out, bge);
  and and_47 (and_47_out, BrLt, bltu);
  and and_48 (and_48_out, not_6_out, bgeu);
  or or_6 (JPCSel, jal, jalr);
  or or_7 (BPCSel, and_43_out, and_44_out, and_45_out, and_46_out, and_47_out, and_48_out);

  // Other names for the same wires on the sheet: opcode[4:0] = Instruction[6:2]; function3[2:0] = Instruction[14:12];
  //   inst25 = Instruction[25]; inst30 = Instruction[30]

  // Notes on the sheet:
  //   INPUTS to your circuit
  //   contents of rom_1 (hex, n*v repeats v):
  //   1041 1141 11c1 1241 1341 13c1 10c1 12c1 16c1 1001 1601 1081 1101 1181 1201 1281 1681 1301 1381 1401
  //   1481 1581 64 74 41 842 2069 2041 1067 17c7
  //   ROM FOR CONTROL LOGIC
  //   DON'T CHANGE THE LOCATIONS OF THE INPUTS AND OUTPUTS!
  //   This is only if you choose to do the ROM option
  //   OUTPUT from your circuit
endmodule
