// Logisim project partial-store.circ as structural Verilog: 1 circuit, main circuit partial_store
module partial_store (
  input  [31:0] Instruction,
  input  [31:0] MemAddress,
  input  [31:0] DataFromReg,
  input  MemRW,
  output [3:0] MemWriteMask,
  output [31:0] DataToMem
);

  wire and_5_out, comparator_1_eq, decoder_1_out0, decoder_1_out1, decoder_1_out2, decoder_1_out3;
  wire [3:0] bit_extender_5_out, multiplexer_1_out, multiplexer_2_out, multiplexer_3_out;
  wire [7:0] and_1_out, and_2_out, and_3_out, and_4_out, bit_extender_1_out, bit_extender_2_out,
       bit_extender_3_out, bit_extender_4_out;
  wire [31:0] multiplexer_4_out;

  Multiplexer #(.select(2), .width(4)) multiplexer_1 (
    .in0(4'b0001), .in1(4'b0010), .in2(4'b0100), .in3(4'b1000), .out(multiplexer_1_out), .sel(MemAddress[1:0]));
  Decoder #(.select(2)) decoder_1 (
    .out0(decoder_1_out0), .out1(decoder_1_out1), .out2(decoder_1_out2), .out3(decoder_1_out3),
    .sel(MemAddress[1:0]), .en(1'b1));
  Multiplexer #(.select(2), .width(4)) multiplexer_2 (
    .in0(4'b0011), .in2(4'b1100), .out(multiplexer_2_out), .sel(MemAddress[1:0]));  // open: in1, in3
  assign bit_extender_1_out = {{7{decoder_1_out1}}, decoder_1_out1};  // Bit_Extender bit_extender_1
  assign bit_extender_2_out = {{7{decoder_1_out3}}, decoder_1_out3};  // Bit_Extender bit_extender_2
  assign bit_extender_3_out = {{7{decoder_1_out0}}, decoder_1_out0};  // Bit_Extender bit_extender_3
  assign bit_extender_4_out = {{7{decoder_1_out2}}, decoder_1_out2};  // Bit_Extender bit_extender_4
  Multiplexer #(.select(2), .width(4)) multiplexer_3 (
    .in0(multiplexer_1_out), .in1(multiplexer_2_out), .in2(4'b1111), .out(multiplexer_3_out),
    .sel(Instruction[13:12]));  // open: in3
  assign and_1_out = DataFromReg[7:0] & bit_extender_3_out;  // AND_Gate and_1, 8 bits wide
  assign and_2_out = DataFromReg[7:0] & bit_extender_1_out;  // AND_Gate and_2, 8 bits wide
  assign and_3_out = DataFromReg[7:0] & bit_extender_4_out;  // AND_Gate and_3, 8 bits wide
  assign and_4_out = DataFromReg[7:0] & bit_extender_2_out;  // AND_Gate and_4, 8 bits wide
  Multiplexer #(.select(2), .width(32)) multiplexer_4 (
    .in0({{16{1'b0}}, DataFromReg[15:0]}), .in1({{8{1'b0}}, DataFromReg[15:0], {8{1'b0}}}),
    .in2({DataFromReg[15:0], {16{1'b0}}}), .out(multiplexer_4_out), .sel(MemAddress[1:0]));  // open: in3
  Comparator #(.width(5)) comparator_1 (.a(Instruction[6:2]), .b(5'b01000), .eq(comparator_1_eq));  // open: gt, lt
  and and_5 (and_5_out, comparator_1_eq, MemRW);
  assign bit_extender_5_out = {{3{and_5_out}}, and_5_out};  // Bit_Extender bit_extender_5
  Multiplexer #(.select(2), .width(32)) multiplexer_5 (
    .in0({and_4_out, and_3_out, and_2_out, and_1_out}), .in1(multiplexer_4_out), .in2(DataFromReg),
    .out(DataToMem), .sel(Instruction[13:12]));  // open: in3
  assign MemWriteMask = bit_extender_5_out & multiplexer_3_out;  // AND_Gate and_6, 4 bits wide

  // Notes on the sheet:
  //   INPUTS to your circuit
  //   DON'T CHANGE THE LOCATIONS OF THE INPUTS AND OUTPUTS!
  //   OUTPUT from your circuit
endmodule
